// Logisim project cpu.circ as structural Verilog: 2 circuits, main circuit main
module main (
  input  [15:0] INSTRUCTION,
  input  CLOCK,
  output [15:0] FETCH_ADDRESS,
  output [15:0] s0_Value,
  output [15:0] s1_Value,
  output [15:0] s2_Value,
  output [15:0] ra_Value,
  output [15:0] sp_Value,
  output [15:0] HI_Value,
  output [15:0] LO_Value
);

  wire and_1_out, and_2_out, and_3_out, and_4_out, beq, bne, eq, eqs, hi_en, j, jr, lh, lo_en, lui,
       main_1_p1, main_1_p3, main_1_p12, main_1_p20, main_2_p1, main_2_p3, main_2_p5, MemToReg, mfHI, mfLO,
       nig, not_1_out, not_2_out, not_3_out, not_4_out, not_5_out, not_6_out, not_7_out, not_8_out,
       not_9_out, or_1_out, or_2_out, or_3_out, or_4_out, or_5_out, or_6_out, or_7_out, sh, which_data,
       which_imm, Write_en;
  wire [2:0] ALUctr, multiplexer_4_out, multiplexer_7_out, multiplexer_10_out, RD, RS, RT;
  wire [5:0] I_imm;
  wire [9:0] bit_extender_6_out, bit_extender_8_out, multiplexer_15_out, multiplexer_16_out, U_imm;
  wire [15:0] adder_1_out, adder_2_out, adder_3_out, adder_5_out, answer, bit_extender_1_out,
       bit_extender_2_out, bit_extender_3_out, bit_extender_4_out, bit_extender_5_out, bit_extender_7_out,
       main_1_p18, main_1_p19, multiplexer_1_out, multiplexer_2_out, multiplexer_3_out, multiplexer_5_out,
       multiplexer_6_out, multiplexer_8_out, multiplexer_9_out, multiplexer_11_out, multiplexer_13_out,
       multiplexer_14_out, Read_Data, register_1_q, result, result2, subtractor_1_out, X, Y;

  and and_1 (and_1_out, beq, eq);
  and and_2 (and_2_out, beq, eq);
  Multiplexer #(.width(16)) multiplexer_1 (
    .in0(INSTRUCTION), .in1({16{1'b0}}), .out(multiplexer_1_out), .sel(or_1_out));  // open: en
  or or_1 (or_1_out, and_1_out, and_3_out, j, jr);
  and and_3 (and_3_out, bne, not_1_out);
  not not_1 (not_1_out, eq);
  not not_2 (not_2_out, eq);
  and and_4 (and_4_out, bne, not_2_out);
  or or_2 (or_2_out, and_2_out, and_4_out);
  not not_3 (not_3_out, or_2_out);
  assign bit_extender_1_out = {{10{I_imm[5]}}, I_imm};  // Bit_Extender bit_extender_1
  Register #(.width(16)) register_1 (.D(multiplexer_1_out), .Q(register_1_q), .clk(CLOCK));  // open: en, clr
  Adder #(.width(16)) adder_1 (.a(bit_extender_1_out), .b(FETCH_ADDRESS), .out(adder_1_out));  // open: cin, cout
  Subtractor #(.width(16)) subtractor_1 (.a(adder_1_out), .b(16'h2), .out(subtractor_1_out));  // open: bin, bout
  Adder #(.width(16)) adder_2 (.a(16'h2), .b(FETCH_ADDRESS), .out(adder_2_out));  // open: cin, cout
  IFU ifu_1 (
    .RS(RS), .RT(RT), .MemToReg(MemToReg), .RD(RD), .Write_En(Write_en), .ALUctr(ALUctr),
    .whichData(which_data), .hi_en(hi_en), .I_imm(I_imm), .U_imm(U_imm), .which_imm(which_imm),
    .lo_en(lo_en), .beq(beq), .bne(bne), .lui(lui), .jr(jr), .j(j), .in_1(register_1_q), .equal(eqs),
    .mfhi(mfHI), .mflo(mfLO), .lh(lh), .sh(sh));
  // Probe on I_imm
  // Probe on main_1_p18
  Multiplexer #(.width(16)) multiplexer_2 (
    .in0(subtractor_1_out), .in1(adder_2_out), .out(multiplexer_2_out), .sel(not_3_out));  // open: en
  or or_3 (or_3_out, jr, j);
  Adder #(.width(16)) adder_3 (.a(main_1_p18), .b(bit_extender_2_out), .out(adder_3_out));  // open: cin, cout
  assign bit_extender_2_out = {{10{I_imm[5]}}, I_imm};  // Bit_Extender bit_extender_2
  not not_4 (not_4_out, j);
  Multiplexer #(.width(16)) multiplexer_3 (
    .in0({FETCH_ADDRESS[15:10], U_imm}), .in1(multiplexer_2_out), .out(multiplexer_3_out), .sel(not_4_out));  // open: en
  or or_4 (or_4_out, beq, bne, or_5_out);
  Multiplexer #(.width(3), .enable("false")) multiplexer_4 (
    .in0(RT), .in1(RD), .out(multiplexer_4_out), .sel(or_4_out));
  Adder #(.width(16)) adder_4 (.a(16'h2), .b(FETCH_ADDRESS));  // open: out, cin, cout
  not not_5 (not_5_out, jr);
  Multiplexer #(.width(16)) multiplexer_5 (
    .in0(adder_3_out), .in1(multiplexer_3_out), .out(multiplexer_5_out), .sel(not_5_out));  // open: en
  not not_6 (not_6_out, lui);
  assign bit_extender_3_out = {{6{1'b0}}, U_imm};  // Bit_Extender bit_extender_3
  Multiplexer #(.width(16)) multiplexer_6 (
    .in0(bit_extender_3_out), .in1(main_1_p18), .out(multiplexer_6_out), .sel(not_6_out));  // open: en
  or or_5 (or_5_out, lh, sh);
  Multiplexer #(.width(3), .enable("false")) multiplexer_7 (
    .in0(multiplexer_4_out), .in1(3'b000), .out(multiplexer_7_out), .sel(sh));
  Multiplexer #(.width(16)) multiplexer_8 (
    .in0(FETCH_ADDRESS), .in1(multiplexer_11_out), .out(multiplexer_8_out), .sel(not_7_out));  // open: en
  not not_7 (not_7_out, or_3_out);
  not not_8 (not_8_out, mfLO);
  Multiplexer #(.width(16)) multiplexer_9 (
    .in0(LO_Value), .in1(multiplexer_6_out), .out(multiplexer_9_out), .sel(not_8_out));  // open: en
  Multiplexer #(.width(3), .enable("false")) multiplexer_10 (.in0(RS), .in1(RD), .out(multiplexer_10_out), .sel(sh));
  Multiplexer #(.width(16)) multiplexer_11 (
    .in0(bit_extender_7_out), .in1(answer), .out(multiplexer_11_out), .sel(which_data));  // open: en
  Register #(.width(16)) PC (.D(multiplexer_5_out), .Q(FETCH_ADDRESS), .clk(CLOCK));  // open: en, clr
  not not_9 (not_9_out, mfHI);
  Multiplexer #(.width(16)) multiplexer_12 (
    .in0(HI_Value), .in1(multiplexer_9_out), .out(X), .sel(not_9_out));  // open: en
  // regfile_main main_1: pin names not known; wires that end beside it: main_1_p1, lui, main_1_p3, multiplexer_10_out, multiplexer_7_out, RD, main_1_p3, s0_Value, multiplexer_8_out, s1_Value, Write_en, main_1_p12, s2_Value, CLOCK, ra_Value, main_1_p12, sp_Value, main_1_p18, main_1_p19, main_1_p20, main_1_p18, main_1_p20
  assign bit_extender_4_out = {{6{multiplexer_16_out[9]}}, multiplexer_16_out};  // Bit_Extender bit_extender_4
  Multiplexer #(.width(16)) multiplexer_13 (
    .in0(main_1_p19), .in1(multiplexer_14_out), .out(multiplexer_13_out), .sel(nig));  // open: en
  Multiplexer #(.width(16), .enable("false")) multiplexer_14 (
    .in0(bit_extender_4_out), .in1(16'h6), .out(multiplexer_14_out), .sel(lui));
  assign bit_extender_5_out = {{13{1'b0}}, RS};  // Bit_Extender bit_extender_5
  assign bit_extender_6_out = {{4{I_imm[5]}}, I_imm};  // Bit_Extender bit_extender_6
  assign bit_extender_7_out = {{6{multiplexer_15_out[9]}}, multiplexer_15_out};  // Bit_Extender bit_extender_7
  Multiplexer #(.width(10)) multiplexer_15 (
    .in0(bit_extender_8_out), .in1(U_imm), .out(multiplexer_15_out), .sel(which_imm));  // open: en
  assign bit_extender_8_out = {{4{I_imm[5]}}, I_imm};  // Bit_Extender bit_extender_8
  or or_6 (or_6_out, mfLO, mfHI);
  Adder #(.width(16)) adder_5 (.a(bit_extender_5_out), .b(bit_extender_4_out), .out(adder_5_out));  // open: cin, cout
  Multiplexer #(.width(10)) multiplexer_16 (
    .in0(bit_extender_6_out), .in1(U_imm), .out(multiplexer_16_out), .sel(which_imm));  // open: en
  Multiplexer #(.width(16)) multiplexer_17 (
    .in0(multiplexer_13_out), .in1({16{1'b0}}), .out(Y), .sel(or_6_out));  // open: en
  // mem_main MEM: pin names not known; wires that end beside it: adder_5_out, result, sh, CLOCK, Read_Data
  Register #(.width(16)) HI (.D(result2), .en(hi_en), .Q(HI_Value), .clk(CLOCK));  // open: clr
  Register #(.width(16)) LO (.D(result), .en(lo_en), .Q(LO_Value), .clk(CLOCK));  // open: clr
  // alu_main main_2: pin names not known; wires that end beside it: main_2_p1, main_2_p1, main_2_p3, main_2_p3, main_2_p5, X, Y, main_2_p5, ALUctr, eq, main_1_p1, result, result2
  // Probe on result
  Multiplexer #(.width(16)) multiplexer_18 (.in0(result), .in1(Read_Data), .out(answer), .sel(MemToReg));  // open: en
  not not_10 (nig, or_7_out);
  or or_7 (or_7_out, beq, eqs, bne);

  // Other names for the same wires on the sheet: clk = CLOCK; fetch_addr[15:0] = FETCH_ADDRESS;
  //   umm[15:0] = {FETCH_ADDRESS[15:10], U_imm}; hi[15:0] = HI_Value; lo[15:0] = LO_Value; ra[15:0] = ra_Value;
  //   s0[15:0] = s0_Value; s1[15:0] = s1_Value; s2[15:0] = s2_Value; sp[15:0] = sp_Value

  // Notes on the sheet:
  //   Output
  //   These are outputs/inputs from run.circ
  //   Inputs
  //   These are DEBUG/TEST outputs from your circuit.
endmodule

module IFU (
  input  [15:0] in_1,
  output [2:0] RS,
  output [2:0] RT,
  output [2:0] RD,
  output equal,
  output [2:0] ALUctr,
  output MemToReg,
  output Write_En,
  output hi_en,
  output lo_en,
  output whichData,
  output which_imm,
  output beq,
  output bne,
  output lui,
  output jr,
  output j,
  output lh,
  output [5:0] I_imm,
  output sh,
  output [9:0] U_imm,
  output mfhi,
  output mflo
);

  wire comparator_3_eq, not_1_out, not_2_out;
  wire [2:0] bit_extender_1_out;

  Comparator #(.width(4)) comparator_1 (.a(in_1[15:12]), .b(4'b1010), .eq(lh));  // open: gt, lt
  Comparator #(.width(4)) comparator_2 (.a(in_1[15:12]), .b(4'b1011), .eq(sh));  // open: gt, lt
  assign bit_extender_1_out = {{1{1'b0}}, in_1[11:10]};  // Bit_Extender bit_extender_1
  not not_1 (not_1_out, comparator_3_eq);
  Comparator #(.width(4)) comparator_3 (.a(in_1[15:12]), .b(4'b0010), .eq(comparator_3_eq));  // open: gt, lt
  Comparator #(.width(4)) comparator_4 (.a(in_1[15:12]), .b(4'b1100), .eq(mfhi));  // open: gt, lt
  Comparator #(.width(4)) comparator_5 (.a(in_1[15:12]), .b(4'b1101), .eq(mflo));  // open: gt, lt
  Multiplexer #(.width(3)) multiplexer_1 (
    .in0(bit_extender_1_out), .in1(in_1[11:9]), .out(RD), .sel(not_1_out));  // open: en
  Comparator #(.width(4)) comparator_6 (.a(in_1[15:12]), .b(4'b0000), .eq(equal));  // open: gt, lt
  // Probe on 14'h240
  // Probe on 14'h2240
  Multiplexer #(.select(3), .width(14)) multiplexer_2 (
    .in0(14'h240), .in1(14'ha40), .in2(14'h1240), .in3(14'h1a40), .in4(14'h2240), .in5(14'h2a40),
    .in6(14'h3240), .in7(14'h39c0),
    .out({ALUctr, MemToReg, Write_En, hi_en, lo_en, whichData, which_imm, beq, bne, lui, jr, j}),
    .sel(in_1[2:0]), .en(equal));
  Multiplexer #(.select(4), .width(14)) multiplexer_3 (
    .in1(14'he4), .in2(14'h221), .in3(14'h2), .in4(14'h10), .in5(14'h8), .in6(14'h1240), .in7(14'h3240),
    .in8(14'h1a40), .in9(14'h2240), .in10(14'h640), .in11(14'h2440), .in12(14'h2240), .in13(14'h22c0),
    .out({ALUctr, MemToReg, Write_En, hi_en, lo_en, whichData, which_imm, beq, bne, lui, jr, j}),
    .sel(in_1[15:12]), .en(not_2_out));  // open: in0, in14, in15
  not not_2 (not_2_out, equal);

  assign I_imm = in_1[5:0];
  assign RS = in_1[8:6];
  assign RT = in_1[5:3];
  assign U_imm = in_1[9:0];

  // Other names for the same wires on the sheet: jawn[2:0] = in_1[11:9]; opcode[3:0] = in_1[15:12];
  //   funct[2:0] = in_1[2:0]
endmodule
